# Fritzing sketch foco (saved by Fritzing 0.9.0b)
breadboards: 1

parts:
  Parte1 = Arduino Uno (Rev3)
  LED1 = smd LED [color="Blue (430nm)" package="0603 [SMD]"]

nets:
  N1: Parte1.D13/SCK, Parte1.GND
  N2: LED1.cathode, LED1.anode
