# Fritzing sketch luces de colores (saved by Fritzing 0.9.0b)
breadboards: 1

parts:
  Parte1 = Arduino Uno (Rev3)
  LED1 = smd LED [color="Blue (525nm)" package="0805 [SMD]"]
  LED1_2 = smd LED [color="Green (565nm)" package="0603 [SMD]"]
  LED2 = smd LED [color="Yellow (574nm)" package="0805 [SMD]"]
  LED3 = smd LED [color="Red (633nm)" package="0805 [SMD]"]
  LED4 = smd LED [color="Orange (620nm)" package="0603 [SMD]"]
  R1 = Resistor [tolerance=±5% resistance=220 package=THT]
  R2 = Resistor [tolerance=±5% resistance=220 package=THT]
  R4 = Resistor [tolerance=±5% resistance=220 package=THT]
  R5 = Resistor [tolerance=±5% resistance=220 package=THT]
  R3 = Resistor [tolerance=±5% resistance=220 package=THT]

nets:
  N1: Parte1.D9_PWM, R1.Pin_1
  N2: Parte1.D10_PWM/SS, R2.Pin_1
  N3: Parte1.D11_PWM/MOSI, R3.Pin_0
  N4: Parte1.D12/MISO, R4.Pin_1
  N5: Parte1.D13/SCK, R5.Pin_1
  N6: Parte1.GND, LED1.cathode, LED1_2.cathode, LED2.cathode, LED3.cathode, LED4.cathode
  N7: LED1.anode, R3.Pin_1
  N8: LED1_2.anode, R4.Pin_0
  N9: LED2.anode, R5.Pin_0
  N10: LED3.anode, R2.Pin_0
  N11: LED4.anode, R1.Pin_0
