# Fritzing sketch servo (saved by Fritzing 0.9.0b)
breadboards: 1

parts:
  J1 = Basic Servo
  Parte1 = Arduino Uno (Rev3)
  LED1 = LED - 5mm [color="Orange (620nm)" package="5 mm [THT]"]
  LED2 = LED - 5mm [color="Red (633nm)" package="5 mm [THT]"]
  LED3 = LED - 5mm [color="Yellow (592nm)" package="5 mm [THT]"]
  R1 = Resistor [tolerance=±5% resistance=220 package=THT]
  R2 = Resistor [tolerance=±5% resistance=220 package=THT]

nets:
  GND: J1.gnd, Parte1.GND, LED1.cathode, LED2.cathode, LED3.cathode
  VCC: J1.vcc, Parte1.5V
  N1: J1.pulse, Parte1.D9_PWM
  N2: Parte1.D11_PWM/MOSI, R2.Pin_1
  N3: Parte1.D12/MISO, R1.Pin_1
  N4: Parte1.D13/SCK, LED2.anode
  N5: LED1.anode, R1.Pin_0
  N6: LED3.anode, R2.Pin_0
